# Fritzing sketch roughsketch (saved by Fritzing 0.9.3b)
breadboards: 1

parts:
  Main_Switch = Toggle Switch [package=THT]
  DC-DC = Mini-360 DC-DC Buck converter [package=THT]
  RELAY = RELAY-2 [package=relay-g5v]
  ESC1 = ESC 30A
  ACM0 = USB connector [package=THT]
  ESC2 = ESC 30A
  ESTOP = Round Pushbutton
  ACM1 = USB connector [package=THT]
  C2 = Electrolytic Capacitor [capacitance=100μF voltage=50V package="0807 [SMD, electrolytic]"]  # not connected
  C3 = Electrolytic Capacitor [capacitance=10µF voltage=50V package="0807 [SMD, electrolytic]"]
  Jetson_Power = Power Jack [package=power_jack_slot]
  Brushless_motor1 = Brushless Motor
  Brushless_motor2 = Brushless Motor
  F1_20A = FUSE [package=fuse_5mm]
  F2_20A = FUSE [package=fuse_5mm]
  USB_HUB = USB connector [package=THT]

nets:
  N1: Main_Switch.L1, RELAY.1, RELAY.10
  36V: Main_Switch.COM
  GND: DC-DC.IN-, ESC1.GND#5, ESC2.GND#5, C3.-, Jetson_Power.GND
  19V: DC-DC.IN+, C3.+, Jetson_Power.PWR
  N2: DC-DC.OUT+, ESTOP.leg0, USB_HUB.chassis5
  N3: DC-DC.OUT-, RELAY.9, USB_HUB.5V
  N4: RELAY.2, ESTOP.leg1
  N5: RELAY.5, F1_20A.1
  N6: RELAY.6, F2_20A.1
  N7: ESC1.v+, ACM0.5V
  N8: ESC1.GND#4, ACM0.chassis5
  N9: ESC1.A, Brushless_motor1.A
  N10: ESC1.B, Brushless_motor1.B
  N11: ESC1.C, Brushless_motor1.C
  N12: ESC1.V+, F1_20A.2
  N13: ESC1.In, ACM0.d-
  N14: ESC2.v+, ACM1.5V
  N15: ESC2.GND#4, ACM1.GND, ACM1.chassis5
  N16: ESC2.A, Brushless_motor2.A
  N17: ESC2.B, Brushless_motor2.B
  N18: ESC2.C, Brushless_motor2.C
  N19: ESC2.V+, F2_20A.2
  N20: ESC2.In, ACM1.d-

custom parts:
  Mini-360 DC-DC Buck converter: Mini-360 DC-DC Buck converter. Tiny buck step down voltage converter, input voltage 4.75 to 23V output 1 to 17V adjustable. Available from ebay and the like.
  ESC 30A: Electronic Speed Controller - 30A
  Brushless Motor: A standard Brushless DC motor
